# Fritzing sketch prototype (saved by Fritzing 0.9.3b)
breadboards: 1

parts:
  U1 = ESP32-38PinWide [part_number=ESP32-38PinWide]  # not connected
  PIR1 = PIR sensor  # not connected
  U2 = GAS_SENSOR [package=mq-3]  # not connected
  J1 = Basic Servo  # not connected
  LED1 = LED - 3mm [color="Red (633nm)" package="3 mm [THT]"]  # not connected
  LED2 = LED - 3mm [color="Red (633nm)" package="3 mm [THT]"]  # not connected
  LED3 = LED - 3mm [color="Red (633nm)" package="3 mm [THT]"]  # not connected
  F1 = Fan - Ventilador [package=THT]
  Part1 = Barometric Pressure Sensor - BMP180 Breakout (GY-68)  # not connected
  Part2 = Jtron 1 Channel Optoisolated Relay Module [package=relay]  # not connected
  M1 = L293D Motor Driver

nets:
  N1: F1.5V, M1.pin_10
  N2: F1.GND, M1.pin_9

custom parts:
  ESP32-38PinWide: Generic 38-Pin ESP32 with wide format (only access to one side of pins on a breadboard) based on Stephen Lilley's HiLetgo ESP-WROOM-32 ESP32 ESP-32S Development Board.
  Fan - Ventilador: Ventilador de 2 pines, se encuentra comunmente en computadoras de escritorio
